# Fritzing sketch 스마트센서등_회로도 (saved by Fritzing 0.9.3b)
breadboards: 1

parts:
  Raspberry_Pi1 = Raspberry Pi B+
  MCP2 = MCP3208
  부품1 = HC-SR501 Body Sensor Module
  Grove2 = Grove Light Sensor
  Mod1 = KY-016 RGB Full Color LED Module [package="Breakout board"]

nets:
  3V3: Raspberry_Pi1.3v3, MCP2.VREF, MCP2.VDD, Grove2.VCC
  N1: Raspberry_Pi1.GPIO10, MCP2.DIN
  N2: Raspberry_Pi1.GPIO9, MCP2.DOUT
  N3: Raspberry_Pi1.GPIO11, MCP2.CLK
  N4: Raspberry_Pi1.GPIO13, Grove2.DO
  N5: Raspberry_Pi1.GPIO19, Mod1.R
  N6: Raspberry_Pi1.GPIO26, 부품1.OUT
  N7: Raspberry_Pi1.GPIO12, Mod1.G
  N8: Raspberry_Pi1.GPIO8, MCP2.CS/SHDN
  GND: Raspberry_Pi1.GND, MCP2.DGND, MCP2.AGND, 부품1.GND, Grove2.GND, Mod1.-
  N9: Raspberry_Pi1.GPIO18, Mod1.B
  5V: Raspberry_Pi1.5V, 부품1.VCC
  N10: MCP2.Chan_0, Grove2.AO

custom parts:
  HC-SR501 Body Sensor Module: Pyroelectric Infrared PIR Motion Sensor Detector Module
  Grove Light Sensor: An analog light sensor
  KY-016 RGB Full Color LED Module: KY-016 Arduino full color 5mm RGB LED, different colors can be obtained by mixing the three primary colors.
